# Fritzing sketch Curiosity_v2 (saved by Fritzing 0.9.3b)

parts:
  BATT1 = 4xAA Switchable Battery Pack w/Bare Wire  # not connected
  U1 = L9110 H-bridge module [part_number="L9110 H-bridge"]
  M1 = DC Motor
  M2 = Dagu DGServo 9g (End View) [part_number=RS001B]  # not connected
  Componente1 = Arduino Uno (Rev3)  # not connected
  Componente2 = Arduino Sensor Shield v5.0
  M3 = DC Motor
  M4 = DC Motor  # not connected
  J3 = Basic Servo
  J4 = Basic Servo
  U2 = L9110 H-bridge module [part_number="L9110 H-bridge"]
  U3 = L9110 H-bridge module [part_number="L9110 H-bridge"]
  M5 = DC Motor
  M6 = DC Motor
  M7 = DC Motor
  J1 = Basic Servo
  J2 = Basic Servo

nets:
  N1: U1.MOTOR_A-A, M7.pin_2
  N2: U1.MOTOR_A-B, M7.pin_1
  N3: M1.pin_1, U3.MOTOR_A-B
  N4: M1.pin_2, U3.MOTOR_A-A
  VCC: Componente2.+5V, J3.vcc, J4.vcc, J1.vcc, J2.vcc
  GND: Componente2.GND, J3.gnd, J4.gnd, J1.gnd, J2.gnd
  N5: M3.pin_1, U2.MOTOR_B-B
  N6: U2.MOTOR_A-A, M6.pin_2
  N7: U2.MOTOR_A-B, M6.pin_1
  N8: U3.MOTOR_B-A, M5.pin_2
  N9: U3.MOTOR_B-B, M5.pin_1

notes:
  Servos:
  Delanteros 13,12
  Traseros 8,7

custom parts:
  4xAA Switchable Battery Pack w/Bare Wire: 4xAA Switchable Battery Pack with Bare Wire connection
